# Fritzing sketch switch_board_0 (saved by Fritzing 0.9.4)
circuit board: 9cm x 5.6cm
breadboards: 1

parts:
  Teensy2 = Teensy++ 2.0
  J2 = screw terminal, 8 pins
  R1 = Resistor [tolerance=±5% resistance=220 package=THT]
  R2 = Resistor [tolerance=±5% resistance=220 package=THT]
  R3 = Resistor [tolerance=±5% resistance=220 package=THT]
  R4 = Resistor [tolerance=±5% resistance=220 package=THT]
  R5 = Resistor [tolerance=±5% resistance=220 package=THT]
  R6 = Resistor [tolerance=±5% resistance=220 package=THT]
  R7 = Resistor [tolerance=±5% resistance=220 package=THT]
  R8 = Resistor [tolerance=±5% resistance=220 package=THT]
  J4 = screw terminal, 8 pins
  J5 = screw terminal, 8 pins
  J3 = female pin header, 4 pins [form="♀ (female)"]

nets:
  N1: Teensy2.GND#0, Teensy2.GND#21, J3.pin3, J3.pin4
  N2: Teensy2.D0, J4.pin8
  N3: Teensy2.D1, J4.pin7
  N4: Teensy2.D2, J4.pin6
  N5: Teensy2.D3, J4.pin5
  N6: Teensy2.D4, J4.pin4
  N7: Teensy2.D5, J4.pin3
  N8: Teensy2.D6, J4.pin2
  N9: Teensy2.D7, J4.pin1
  N10: Teensy2.C0, J5.pin8
  N11: Teensy2.C1, J5.pin7
  N12: Teensy2.C2, J5.pin6
  N13: Teensy2.C3, J5.pin5
  N14: Teensy2.C4, J5.pin4
  N15: Teensy2.C5, J5.pin3
  N16: Teensy2.C6, J5.pin2
  N17: Teensy2.C7, J5.pin1
  N18: Teensy2.F7, J2.pin8, R2.Pin_1
  N19: Teensy2.F6, Teensy2.F0, Teensy2.GND#32, J2.pin1, J2.pin7, R1.Pin_0, R1.Pin_1, R2.Pin_0, R3.Pin_0, R4.Pin_0, R5.Pin_0, R6.Pin_0, R6.Pin_1, R7.Pin_0, R8.Pin_0
  N20: Teensy2.F5, J2.pin6, R7.Pin_1
  N21: Teensy2.F4, J2.pin5, R8.Pin_1
  N22: Teensy2.F3, J2.pin4, R5.Pin_1
  N23: Teensy2.F2, J2.pin3, R4.Pin_1
  N24: Teensy2.F1, J2.pin2, R3.Pin_1
  N25: Teensy2.VCC, J3.pin1, J3.pin2
